// Logisim project RV32 PROCESSOR LOGISM SIMULATION.circ as structural Verilog: 14 circuits, main circuit Decoder
module Decoder (
  input  [6:0] in_1,
  output R_Type,
  output I_Type_lw,
  output I_Type_addi,
  output I_Type_jalr,
  output S_Type,
  output SB_Type,
  output U_Type_AUIPC,
  output U_Type_LUI,
  output UJ_Type
);

  Comparator #(.width(7)) comparator_1 (.a(in_1), .b(7'b0110011), .eq(R_Type));  // open: gt, lt
  Comparator #(.width(7)) comparator_2 (.a(in_1), .b(7'b0000011), .eq(I_Type_lw));  // open: gt, lt
  Comparator #(.width(7)) comparator_3 (.a(in_1), .b(7'b0010011), .eq(I_Type_addi));  // open: gt, lt
  Comparator #(.width(7)) comparator_4 (.a(in_1), .b(7'b1100111), .eq(I_Type_jalr));  // open: gt, lt
  Comparator #(.width(7)) comparator_5 (.a(in_1), .b(7'b0100011), .eq(S_Type));  // open: gt, lt
  Comparator #(.width(7)) comparator_6 (.a(in_1), .b(7'b1100011), .eq(SB_Type));  // open: gt, lt
  Comparator #(.width(7)) comparator_7 (.a(in_1), .b(7'b0010111), .eq(U_Type_AUIPC));  // open: gt, lt
  Comparator #(.width(7)) comparator_8 (.a(in_1), .b(7'b0110111), .eq(U_Type_LUI));  // open: gt, lt
  Comparator #(.width(7)) comparator_9 (.a(in_1), .b(7'b1101111), .eq(UJ_Type));  // open: gt, lt
endmodule

module imm_gen (
  input  [31:0] INS,
  input  [31:0] in_2,
  output [31:0] out_3,
  output [31:0] out_4,
  output [31:0] out_5,
  output [31:0] out_6,
  output [31:0] out_7
);

  wire [19:0] shifter_1_out;
  wire [31:0] bit_extender_3_out, bit_extender_4_out;

  assign out_3 = {{20{1'b0}}, INS[31:20]};  // Bit_Extender bit_extender_1
  assign out_4 = {{20{1'b0}}, {INS[31:25], INS[11:7]}};  // Bit_Extender bit_extender_2
  assign bit_extender_3_out = {{19{1'b0}}, {INS[31], INS[7], INS[30:25], INS[11:8], 1'b0}};  // Bit_Extender bit_extender_3
  assign bit_extender_4_out = {{11{1'b0}}, {INS[31], INS[19:12], INS[20], INS[30:21], 1'b0}};  // Bit_Extender bit_extender_4
  Shifter #(.width(20)) shifter_1 (.in(INS[31:12]), .\dist (5'b01100), .out(shifter_1_out));
  assign out_7 = {{12{1'b0}}, shifter_1_out};  // Bit_Extender bit_extender_5
  Adder #(.width(32)) adder_1 (.a(bit_extender_3_out), .b(in_2), .out(out_5));  // open: cin, cout
  Adder #(.width(32)) adder_2 (.a(bit_extender_4_out), .b(in_2), .out(out_6));  // open: cin, cout

  // Notes on the sheet:
  //   PC
  //   I
  //   SB
  //   UJ
  //   U
  //   S
endmodule

module CONTROL_DECODE (
  input  R_Type,
  input  I_Type,
  input  Load,
  input  JALR,
  input  Store,
  input  Branch,
  input  Auipc,
  input  Lui,
  input  JAL,
  input  [2:0] fn_3_inp,
  input  fun_7_inp,
  output REG_Write,
  output Branch_2,
  output load_2,
  output Store_2,
  output Mem_2_Reg,
  output [1:0] Operand_A,
  output operang_B,
  output [1:0] IMM_SELECTOR,
  output [1:0] NEXT_PC,
  output [3:0] out_21
);

  wire or_1_out, or_2_out;
  wire [2:0] alu_1_output2;

  or or_1 (or_1_out, Auipc, Lui);
  or or_2 (or_2_out, R_Type, I_Type, Load, JALR, Store, Branch);
  or or_3 (REG_Write, I_Type, Load, JALR, R_Type, Auipc, Lui, JAL);
  OP_A op_a_1 (.rs1(or_2_out), .pc(Auipc), .pc_4(JAL), .zero(1'b0), .a(Operand_A[1]), .b(Operand_A[0]));
  or or_4 (operang_B, I_Type, Branch, Store);
  IMM imm_1 (.Itype(I_Type), .STYPE(Store), .UTYPE(or_1_out), .a(IMM_SELECTOR[1]), .b(IMM_SELECTOR[0]));
  NEXT_PC_SEL next_pc_sel_1 (.SBTYPE(Branch), .JALR(JALR), .JAL(JAL), .a(NEXT_PC[1]), .b(NEXT_PC[0]));
  ALU alu_1 (
    .Rtype(R_Type), .Itype(I_Type), .load(Load), .jalr(JALR), .store(Store), .Auipc(Auipc), .Lui(Lui),
    .jal(JAL), .output0(alu_1_output2[2]), .output1(alu_1_output2[1]), .output2(alu_1_output2[0]));
  alu_control alu_control_1 (
    .opc0(alu_1_output2[2]), .opc1(alu_1_output2[1]), .opc2(alu_1_output2[0]), .fn3_0(fn_3_inp[2]),
    .fn3_1(fn_3_inp[1]), .fn3_2(fn_3_inp[0]), .fn7(fun_7_inp), .outp0(out_21[3]), .outp1(out_21[2]),
    .outp2(out_21[1]), .outp3(out_21[0]));

  assign Branch_2 = Branch;
  assign load_2 = Load;
  assign Mem_2_Reg = Load;
  assign Store_2 = Store;
endmodule

module IMM (
  input  Itype,
  input  STYPE,
  input  UTYPE,
  output a,
  output b
);

  wire not_1_out, not_2_out, not_3_out;

  not not_1 (not_1_out, Itype);
  not not_2 (not_2_out, STYPE);
  not not_3 (not_3_out, Itype);
  and and_1 (a, not_1_out, not_2_out, UTYPE);
  and and_2 (b, not_3_out, STYPE);
endmodule

module NEXT_PC_SEL (
  input  SBTYPE,
  input  JALR,
  input  JAL,
  output a,
  output b
);

  or or_1 (a, JALR, SBTYPE);
  or or_2 (b, JAL, SBTYPE);
endmodule

module OP_A (
  input  rs1,
  input  pc,
  input  pc_4,
  input  zero,
  output a,
  output b
);

  wire not_1_out, not_2_out, not_3_out, not_4_out;

  not not_1 (not_1_out, rs1);
  and and_1 (a, not_1_out, not_2_out);
  not not_2 (not_2_out, pc);
  not not_3 (not_3_out, rs1);
  and and_2 (b, not_3_out, not_4_out);
  not not_4 (not_4_out, pc_4);
endmodule

module ALU (
  input  Rtype,
  input  Itype,
  input  load,
  input  jalr,
  input  store,
  input  Auipc,
  input  Lui,
  input  jal,
  output output0,
  output output1,
  output output2
);

  wire or_1_out, or_2_out, or_3_out, or_4_out, or_5_out, or_6_out;

  or or_1 (or_1_out, jal, Auipc);
  or or_2 (or_2_out, store, Itype);
  or or_3 (or_3_out, jal, Lui);
  or or_4 (or_4_out, Auipc, jalr);
  or or_5 (or_5_out, jal, store);
  or or_6 (or_6_out, jalr, load);
  or or_7 (output0, or_1_out, or_2_out);
  or or_8 (output1, or_3_out, or_4_out);
  or or_9 (output2, or_5_out, or_6_out);
endmodule

module aluopp (
  input  [31:0] in_1,
  input  [31:0] in_2,
  input  [3:0] in_3,
  output [31:0] out_4
);

  wire comparator_1_lt, comparator_2_lt;
  wire [31:0] adder_1_out, and_1_out, bit_extender_1_out, bit_extender_2_out, or_1_out, shifter_1_out,
       shifter_2_out, shifter_3_out, subtractor_1_out, xor_1_out;

  Adder #(.width(32)) adder_1 (.a(in_1), .b(in_2), .out(adder_1_out));  // open: cin, cout
  Subtractor #(.width(32)) subtractor_1 (.a(in_1), .b(in_2), .out(subtractor_1_out));  // open: bin, bout
  assign and_1_out = in_1 & in_2;  // AND_Gate and_1, 32 bits wide
  assign or_1_out = in_1 | in_2;  // OR_Gate or_1, 32 bits wide
  assign xor_1_out = in_1 ^ in_2;  // XOR_Gate xor_1, 32 bits wide
  Shifter #(.width(32)) shifter_1 (.in(in_1), .\dist (in_2[4:0]), .out(shifter_1_out));
  Shifter #(.width(32), .shift("lr")) shifter_2 (.in(in_1), .\dist (in_2[4:0]), .out(shifter_2_out));
  Shifter #(.width(32), .shift("ar")) shifter_3 (.in(in_1), .\dist (in_2[4:0]), .out(shifter_3_out));
  Comparator #(.width(32)) comparator_1 (.a(in_1), .b(in_2), .lt(comparator_1_lt));  // open: gt, eq
  Comparator #(.width(32), .mode("unsigned")) comparator_2 (.a(in_1), .b(in_2), .lt(comparator_2_lt));  // open: gt, eq
  assign bit_extender_1_out = {{31{1'b0}}, comparator_1_lt};  // Bit_Extender bit_extender_1
  assign bit_extender_2_out = {{31{1'b0}}, comparator_2_lt};  // Bit_Extender bit_extender_2
  Multiplexer #(.select(4), .width(32)) multiplexer_1 (
    .in0(adder_1_out), .in1(subtractor_1_out), .in2(and_1_out), .in3(or_1_out), .in4(xor_1_out),
    .in5(shifter_1_out), .in6(shifter_2_out), .in7(bit_extender_1_out), .in8(bit_extender_2_out),
    .in9(shifter_3_out), .in15(in_1), .out(out_4), .sel(in_3));  // open: in10, in11, in12, in13, in14, en

  // Notes on the sheet:
  //   op_A
  //   op_B
  //   com
  //   un com
endmodule

module alu_control (
  input  opc0,
  input  opc1,
  input  opc2,
  input  fn3_0,
  input  fn3_1,
  input  fn3_2,
  input  fn7,
  output outp0,
  output outp1,
  output outp2,
  output outp3
);

  wire and_1_out, and_2_out, and_3_out, and_4_out, and_5_out, and_6_out, and_7_out, and_8_out, and_9_out,
       and_10_out, and_11_out, and_12_out, and_13_out, and_14_out, and_15_out, and_16_out, and_17_out,
       not_1_out, not_2_out, not_3_out, not_4_out, not_5_out, not_6_out, not_7_out, not_8_out, not_9_out,
       not_10_out, not_11_out, not_12_out, not_13_out, not_14_out, not_15_out, not_16_out, not_17_out,
       not_18_out, not_19_out, not_20_out, not_21_out, not_22_out, not_23_out, not_24_out, not_25_out,
       not_26_out, not_27_out, not_28_out, not_29_out, not_30_out, not_31_out, not_32_out, not_33_out,
       not_34_out, not_35_out, not_36_out, not_37_out, not_38_out, not_39_out, not_40_out, not_41_out;

  not not_1 (not_1_out, opc0);
  not not_2 (not_2_out, fn3_1);
  not not_3 (not_3_out, opc0);
  not not_4 (not_4_out, fn3_0);
  not not_5 (not_5_out, opc0);
  not not_6 (not_6_out, opc0);
  not not_7 (not_7_out, fn3_1);
  not not_8 (not_8_out, fn7);
  not not_9 (not_9_out, opc0);
  not not_10 (not_10_out, opc2);
  not not_11 (not_11_out, fn3_0);
  not not_12 (not_12_out, fn3_2);
  not not_13 (not_13_out, opc0);
  not not_14 (not_14_out, fn3_1);
  not not_15 (not_15_out, fn3_2);
  not not_16 (not_16_out, opc0);
  not not_17 (not_17_out, fn3_1);
  not not_18 (not_18_out, fn3_2);
  not not_19 (not_19_out, opc0);
  not not_20 (not_20_out, opc2);
  not not_21 (not_21_out, fn3_2);
  not not_22 (not_22_out, opc0);
  not not_23 (not_23_out, fn7);
  not not_24 (not_24_out, opc0);
  not not_25 (not_25_out, opc0);
  not not_26 (not_26_out, opc1);
  not not_27 (not_27_out, opc2);
  not not_28 (not_28_out, opc1);
  not not_29 (not_29_out, opc2);
  not not_30 (not_30_out, fn3_1);
  not not_31 (not_31_out, opc0);
  not not_32 (not_32_out, fn3_0);
  not not_33 (not_33_out, fn3_1);
  not not_34 (not_34_out, opc0);
  not not_35 (not_35_out, fn3_1);
  not not_36 (not_36_out, opc0);
  not not_37 (not_37_out, opc2);
  not not_38 (not_38_out, fn3_2);
  not not_39 (not_39_out, opc0);
  not not_40 (not_40_out, fn3_0);
  not not_41 (not_41_out, fn3_1);
  and and_1 (and_1_out, not_1_out, not_2_out, fn3_2, fn7);
  and and_2 (and_2_out, not_3_out, not_4_out, fn3_1, fn3_2);
  and and_3 (and_3_out, not_5_out, opc1, opc2);
  and and_4 (and_4_out, not_6_out, not_7_out, fn3_2, not_8_out);
  and and_5 (and_5_out, not_9_out, not_10_out, not_11_out, fn3_1, not_12_out);
  and and_6 (and_6_out, not_13_out, fn3_0, not_14_out, not_15_out);
  and and_7 (and_7_out, not_16_out, opc1, not_17_out, not_18_out);
  and and_8 (and_8_out, not_19_out, not_20_out, fn3_1, not_21_out);
  and and_9 (and_9_out, not_22_out, fn3_0, fn3_2, not_23_out);
  and and_10 (and_10_out, not_24_out, fn3_0, fn3_1);
  and and_11 (and_11_out, not_25_out, opc1, opc2);
  and and_12 (and_12_out, opc0, not_26_out, not_27_out, fn3_0);
  and and_13 (and_13_out, not_28_out, not_29_out, not_30_out, fn7);
  and and_14 (and_14_out, not_31_out, not_32_out, not_33_out, fn3_2);
  and and_15 (and_15_out, not_34_out, not_35_out, fn3_2, fn7);
  and and_16 (and_16_out, not_36_out, not_37_out, fn3_1, not_38_out);
  and and_17 (and_17_out, not_39_out, opc1, not_40_out, not_41_out);
  or or_1 (outp0, and_1_out, and_2_out, and_3_out);
  or or_2 (outp1, and_4_out, and_5_out, and_6_out, and_7_out);
  or or_3 (outp2, and_8_out, and_9_out, and_10_out, and_11_out, and_12_out);
  or or_4 (outp3, and_13_out, and_14_out, and_15_out, and_16_out, and_17_out);
endmodule

module control_unit (
  input  [6:0] in_1,
  input  [2:0] in_2,
  input  FN_7,
  output REG_Write,
  output Branch,
  output Store,
  output Mem_2_Reg,
  output [1:0] Operand_A,
  output operang_B,
  output [1:0] IMM_SELECTOR,
  output [1:0] NEXT_PC,
  output load,
  output [3:0] alu_op_sel
);

  wire type_decoder_1_i_type_addi, type_decoder_1_i_type_jalr, type_decoder_1_i_type_lw,
       type_decoder_1_r_type, type_decoder_1_s_type, type_decoder_1_sb_type, type_decoder_1_u_type_auipc,
       type_decoder_1_u_type_lui, type_decoder_1_uj_type;

  type_decoder type_decoder_1 (
    .in_1(in_1), .R_Type(type_decoder_1_r_type), .I_Type_lw(type_decoder_1_i_type_lw),
    .I_Type_addi(type_decoder_1_i_type_addi), .I_Type_jalr(type_decoder_1_i_type_jalr),
    .S_Type(type_decoder_1_s_type), .SB_Type(type_decoder_1_sb_type),
    .U_Type_AUIPC(type_decoder_1_u_type_auipc), .U_Type_LUI(type_decoder_1_u_type_lui),
    .UJ_Type(type_decoder_1_uj_type));
  CONTROL_DECODE control_decode_1 (
    .REG_Write(REG_Write), .Branch_2(Branch), .Store_2(Store), .Mem_2_Reg(Mem_2_Reg), .Operand_A(Operand_A),
    .operang_B(operang_B), .IMM_SELECTOR(IMM_SELECTOR), .NEXT_PC(NEXT_PC), .R_Type(type_decoder_1_r_type),
    .I_Type(type_decoder_1_i_type_lw), .Load(type_decoder_1_i_type_addi), .JALR(type_decoder_1_i_type_jalr),
    .Store(type_decoder_1_s_type), .Branch(type_decoder_1_sb_type), .Auipc(type_decoder_1_u_type_auipc),
    .Lui(type_decoder_1_u_type_lui), .JAL(type_decoder_1_uj_type), .fun_7_inp(FN_7), .out_21(alu_op_sel),
    .fn_3_inp(in_2), .load_2(load));
endmodule

module type_decoder (
  input  [6:0] in_1,
  output R_Type,
  output I_Type_lw,
  output I_Type_addi,
  output I_Type_jalr,
  output S_Type,
  output SB_Type,
  output U_Type_AUIPC,
  output U_Type_LUI,
  output UJ_Type
);

  wire comparator_1_eq, comparator_2_eq;

  Comparator #(.width(7)) comparator_1 (.a(in_1), .b(7'b0110011), .eq(comparator_1_eq));  // open: gt, lt
  Comparator #(.width(7)) comparator_2 (.a(in_1), .b(7'b0111011), .eq(comparator_2_eq));  // open: gt, lt
  Comparator #(.width(7)) comparator_3 (.a(in_1), .b(7'b0010011), .eq(I_Type_lw));  // open: gt, lt
  Comparator #(.width(7)) comparator_4 (.a(in_1), .b(7'b0000011), .eq(I_Type_addi));  // open: gt, lt
  Comparator #(.width(7)) comparator_5 (.a(in_1), .b(7'b1100111), .eq(I_Type_jalr));  // open: gt, lt
  Comparator #(.width(7)) comparator_6 (.a(in_1), .b(7'b0100011), .eq(S_Type));  // open: gt, lt
  Comparator #(.width(7)) comparator_7 (.a(in_1), .b(7'b1100011), .eq(SB_Type));  // open: gt, lt
  Comparator #(.width(7)) comparator_8 (.a(in_1), .b(7'b0010111), .eq(U_Type_AUIPC));  // open: gt, lt
  Comparator #(.width(7)) comparator_9 (.a(in_1), .b(7'b0110111), .eq(U_Type_LUI));  // open: gt, lt
  Comparator #(.width(7)) comparator_10 (.a(in_1), .b(7'b1101111), .eq(UJ_Type));  // open: gt, lt
  or or_1 (R_Type, comparator_1_eq, comparator_2_eq);
endmodule

module BRANCH (
  input  [31:0] in_1,
  input  ENABLE,
  input  [2:0] FN_3,
  input  [31:0] in_4,
  output BRANCH_OUT
);

  wire comparator_1_eq, comparator_2_eq, comparator_3_lt, comparator_4_eq, comparator_4_gt, comparator_5_lt,
       comparator_6_eq, comparator_6_gt, not_1_out, or_1_out, or_2_out;

  Comparator #(.width(32)) comparator_1 (.a(in_1), .b(in_4), .eq(comparator_1_eq));  // open: gt, lt
  Comparator #(.width(32)) comparator_2 (.a(in_1), .b(in_4), .eq(comparator_2_eq));  // open: gt, lt
  Comparator #(.width(32)) comparator_3 (.a(in_1), .b(in_4), .lt(comparator_3_lt));  // open: gt, eq
  Comparator #(.width(32)) comparator_4 (.a(in_1), .b(in_4), .gt(comparator_4_gt), .eq(comparator_4_eq));  // open: lt
  Comparator #(.width(32), .mode("unsigned")) comparator_5 (.a(in_1), .b(in_4), .lt(comparator_5_lt));  // open: gt, eq
  Comparator #(.width(32), .mode("unsigned")) comparator_6 (
    .a(in_1), .b(in_4), .gt(comparator_6_gt), .eq(comparator_6_eq));  // open: lt
  not not_1 (not_1_out, comparator_2_eq);
  or or_1 (or_1_out, comparator_4_gt, comparator_4_eq);
  or or_2 (or_2_out, comparator_6_gt, comparator_6_eq);
  Multiplexer #(.select(3)) multiplexer_1 (
    .in0(comparator_1_eq), .in1(not_1_out), .in4(comparator_3_lt), .in5(or_1_out), .in6(comparator_5_lt),
    .in7(or_2_out), .out(BRANCH_OUT), .sel(FN_3), .en(ENABLE));  // open: in2, in3

  // Notes on the sheet:
  //   RS1
  //   RS2
  //   beg
  //   bne
  //   blt
  //   bge
  //   bltu
  //   bgeu
endmodule

// NEXT PC SEL
module main1 (
  output [1:0] out_1,
  output [31:0] out_2,
  output [31:0] out_3,
  output [31:0] out_4,
  output [31:0] out_5,
  output [31:0] out_6,
  output [31:0] out_7,
  output [4:0] out_8,
  output out_9,
  output [11:0] out_10,
  output [31:0] out_11
);

  wire branch_1_branch_out, button_1_out, clock_1_out, control_unit_1_branch, control_unit_1_store, OP_B,
       REG_W, RESET_2_out, RESET_out, undriven;
  wire [1:0] IMM_SEL, OP_A;
  wire [2:0] rom_1_data_2;
  wire [3:0] control_unit_1_alu_op_sel;
  wire [31:0] adder_2_out, I, imm_gen_1_out_4, imm_gen_1_out_7, multiplexer_1_out, multiplexer_2_out,
       multiplexer_3_out, multiplexer_4_out, multiplexer_5_out, PC, PC_4, ram_1_data,
       regester_file_32_1_out_9, rom_1_data, SB;

  Clock clock_1 (.out(clock_1_out));
  Button RESET (.out(RESET_out));
  Register #(.width(32)) register_1 (.D(multiplexer_1_out), .Q(PC), .clk(clock_1_out), .clr(RESET_out));  // open: en
  Multiplexer #(.select(2), .width(32)) multiplexer_1 (
    .in0(PC_4), .in1(out_11), .in2(adder_2_out), .in3(multiplexer_2_out), .out(multiplexer_1_out), .sel(out_1));  // open: en
  Adder #(.width(32)) adder_1 (.a(PC), .b(32'h4), .out(PC_4));  // open: cin, cout
  BRANCH branch_1 (
    .in_1(regester_file_32_1_out_9), .in_4(out_2), .BRANCH_OUT(branch_1_branch_out), .FN_3(rom_1_data_2),
    .ENABLE(control_unit_1_branch));
  Button button_1 (.out(button_1_out));
  Multiplexer #(.width(32)) multiplexer_2 (
    .in0(PC_4), .in1(SB), .out(multiplexer_2_out), .sel(branch_1_branch_out));  // open: en
  ROM #(.addrWidth(12), .dataWidth(32)) rom_1 (
    .addr(PC[13:2]), .data({rom_1_data[31:15], rom_1_data_2, out_8, rom_1_data[6:0]}));  // open: sel
  regester_file_32 regester_file_32_1 (
    .out_9(regester_file_32_1_out_9), .out_10(out_2), .in_1(out_3), .in_7(clock_1_out),
    .in_4(rom_1_data[19:15]), .in_6(rom_1_data[24:20]), .in_3(REG_W), .in_5(out_8), .in_2(button_1_out));  // open: out_8
  imm_gen imm_gen_1 (
    .INS({rom_1_data[31:15], rom_1_data_2, out_8, rom_1_data[6:0]}), .in_2(PC), .out_3(I),
    .out_4(imm_gen_1_out_4), .out_5(SB), .out_6(out_11), .out_7(imm_gen_1_out_7));
  Adder #(.width(32)) adder_2 (.a(I), .b(regester_file_32_1_out_9), .out(adder_2_out));  // open: cin, cout
  control_unit control_unit_1 (
    .REG_Write(REG_W), .Branch(control_unit_1_branch), .Store(control_unit_1_store), .Operand_A(OP_A),
    .operang_B(OP_B), .IMM_SELECTOR(IMM_SEL), .NEXT_PC(out_1), .alu_op_sel(control_unit_1_alu_op_sel),
    .in_1(rom_1_data[6:0]), .in_2(rom_1_data_2), .FN_7(rom_1_data[30]), .load(out_9));  // open: Mem_2_Reg
  Multiplexer #(.select(2), .width(32)) multiplexer_3 (
    .in0(regester_file_32_1_out_9), .in1(PC), .in2(PC_4), .in3({32{1'b0}}), .out(multiplexer_3_out),
    .sel(OP_A));  // open: en
  Multiplexer #(.width(32)) multiplexer_4 (
    .in0(out_2), .in1(multiplexer_5_out), .out(multiplexer_4_out), .sel(OP_B));  // open: en
  Multiplexer #(.select(2), .width(32)) multiplexer_5 (
    .in0(I), .in1(imm_gen_1_out_4), .in2(imm_gen_1_out_7), .out(multiplexer_5_out), .sel(IMM_SEL));  // open: in3, en
  aluopp aluopp_1 (.in_1(multiplexer_3_out), .in_2(multiplexer_4_out), .in_3(control_unit_1_alu_op_sel), .out_4(out_6));
  RAM #(.addrWidth(12), .dataWidth(32), .bus("separate")) ram_1 (
    .addr(out_6[13:2]), .din(out_2), .data(ram_1_data), .str(control_unit_1_store), .sel(undriven),
    .clk(clock_1_out), .ld(out_9), .clr(RESET_2_out));
  Multiplexer #(.width(32)) multiplexer_6 (.in0(out_6), .in1(ram_1_data), .out(out_3), .sel(out_9));  // open: en
  Button RESET_2 (.out(RESET_2_out));

  assign out_4 = out_3;
  assign out_5 = out_2;
  assign out_7 = out_2;
  assign out_10 = out_6[13:2];

  // Other names for the same wires on the sheet: DM_TO_REG[31:0] = out_3; NEXT_PC_SEL[1:0] = out_1; UJ[31:0] = out_11

  // Notes on the sheet:
  //   RV 32 Logiaim Software by KHALIL REHMAN
  //   contents of rom_1 (hex, n*v repeats v):
  //   500293 a00313 502023 2303
endmodule

module regester_file_32 (
  input  [31:0] in_1,
  input  in_2,
  input  in_3,
  input  [4:0] in_4,
  input  [4:0] in_5,
  input  [4:0] in_6,
  input  in_7,
  output [31:0] out_8,
  output [31:0] out_9,
  output [31:0] out_10
);

  wire decoder_1_out0, decoder_1_out1, decoder_1_out2, decoder_1_out3, decoder_1_out4, decoder_1_out5,
       decoder_1_out6, decoder_1_out7, decoder_1_out8, decoder_1_out9, decoder_1_out10, decoder_1_out11,
       decoder_1_out12, decoder_1_out13, decoder_1_out14, decoder_1_out15, decoder_1_out16, decoder_1_out17,
       decoder_1_out18, decoder_1_out19, decoder_1_out20, decoder_1_out21, decoder_1_out22, decoder_1_out23,
       decoder_1_out24, decoder_1_out25, decoder_1_out26, decoder_1_out27, decoder_1_out28, decoder_1_out29,
       decoder_1_out30, decoder_1_out31;
  wire [31:0] register_1_q, register_2_q, register_3_q, register_4_q, register_6_q, register_7_q,
       register_8_q, register_9_q, register_10_q, register_11_q, register_12_q, register_13_q, register_14_q,
       register_15_q, register_16_q, register_17_q, register_18_q, register_19_q, register_20_q,
       register_21_q, register_22_q, register_23_q, register_24_q, register_25_q, register_26_q,
       register_27_q, register_28_q, register_29_q, register_30_q, register_31_q;

  Decoder_part #(.select(5), .disabled(0)) decoder_1 (
    .out0(decoder_1_out0), .out1(decoder_1_out1), .out2(decoder_1_out2), .out3(decoder_1_out3),
    .out4(decoder_1_out4), .out5(decoder_1_out5), .out6(decoder_1_out6), .out7(decoder_1_out7),
    .out8(decoder_1_out8), .out9(decoder_1_out9), .out10(decoder_1_out10), .out11(decoder_1_out11),
    .out12(decoder_1_out12), .out13(decoder_1_out13), .out14(decoder_1_out14), .out15(decoder_1_out15),
    .out16(decoder_1_out16), .out17(decoder_1_out17), .out18(decoder_1_out18), .out19(decoder_1_out19),
    .out20(decoder_1_out20), .out21(decoder_1_out21), .out22(decoder_1_out22), .out23(decoder_1_out23),
    .out24(decoder_1_out24), .out25(decoder_1_out25), .out26(decoder_1_out26), .out27(decoder_1_out27),
    .out28(decoder_1_out28), .out29(decoder_1_out29), .out30(decoder_1_out30), .out31(decoder_1_out31),
    .sel(in_5), .en(in_3));
  Register #(.width(32)) register_1 (.D(in_1), .en(decoder_1_out1), .Q(register_1_q), .clk(in_7), .clr(in_2));
  Register #(.width(32)) register_2 (.D(in_1), .en(decoder_1_out2), .Q(register_2_q), .clk(in_7), .clr(in_2));
  Register #(.width(32)) register_3 (.D(in_1), .en(decoder_1_out3), .Q(register_3_q), .clk(in_7), .clr(in_2));
  Register #(.width(32)) register_4 (.D(in_1), .en(decoder_1_out4), .Q(register_4_q), .clk(in_7), .clr(in_2));
  Register #(.width(32)) register_5 (.D(in_1), .en(decoder_1_out5), .Q(out_8), .clk(in_7), .clr(in_2));
  Register #(.width(32)) register_6 (.D(in_1), .en(decoder_1_out6), .Q(register_6_q), .clk(in_7), .clr(in_2));
  Register #(.width(32)) register_7 (.D(in_1), .en(decoder_1_out7), .Q(register_7_q), .clk(in_7), .clr(in_2));
  Register #(.width(32)) register_8 (.D(in_1), .en(decoder_1_out8), .Q(register_8_q), .clk(in_7), .clr(in_2));
  Register #(.width(32)) register_9 (.D(in_1), .en(decoder_1_out9), .Q(register_9_q), .clk(in_7), .clr(in_2));
  Register #(.width(32)) register_10 (.D(in_1), .en(decoder_1_out10), .Q(register_10_q), .clk(in_7), .clr(in_2));
  Register #(.width(32)) register_11 (.D(in_1), .en(decoder_1_out11), .Q(register_11_q), .clk(in_7), .clr(in_2));
  Register #(.width(32)) register_12 (.D(in_1), .en(decoder_1_out12), .Q(register_12_q), .clk(in_7), .clr(in_2));
  Register #(.width(32)) register_13 (.D(in_1), .en(decoder_1_out13), .Q(register_13_q), .clk(in_7), .clr(in_2));
  Register #(.width(32)) register_14 (.D(in_1), .en(decoder_1_out14), .Q(register_14_q), .clk(in_7), .clr(in_2));
  Register #(.width(32)) register_15 (.D(in_1), .en(decoder_1_out15), .Q(register_15_q), .clk(in_7), .clr(in_2));
  Register #(.width(32)) register_16 (.D(in_1), .en(decoder_1_out16), .Q(register_16_q), .clk(in_7), .clr(in_2));
  Register #(.width(32)) register_17 (.D(in_1), .en(decoder_1_out17), .Q(register_17_q), .clk(in_7), .clr(in_2));
  Register #(.width(32)) register_18 (.D(in_1), .en(decoder_1_out18), .Q(register_18_q), .clk(in_7), .clr(in_2));
  Register #(.width(32)) register_19 (.D(in_1), .en(decoder_1_out19), .Q(register_19_q), .clk(in_7), .clr(in_2));
  Register #(.width(32)) register_20 (.D(in_1), .en(decoder_1_out20), .Q(register_20_q), .clk(in_7), .clr(in_2));
  Register #(.width(32)) register_21 (.D(in_1), .en(decoder_1_out21), .Q(register_21_q), .clk(in_7), .clr(in_2));
  Register #(.width(32)) register_22 (.D(in_1), .en(decoder_1_out22), .Q(register_22_q), .clk(in_7), .clr(in_2));
  Register #(.width(32)) register_23 (.D(in_1), .en(decoder_1_out23), .Q(register_23_q), .clk(in_7), .clr(in_2));
  Register #(.width(32)) register_24 (.D(in_1), .en(decoder_1_out24), .Q(register_24_q), .clk(in_7), .clr(in_2));
  Register #(.width(32)) register_25 (.D(in_1), .en(decoder_1_out25), .Q(register_25_q), .clk(in_7), .clr(in_2));
  Register #(.width(32)) register_26 (.D(in_1), .en(decoder_1_out26), .Q(register_26_q), .clk(in_7), .clr(in_2));
  Register #(.width(32)) register_27 (.D(in_1), .en(decoder_1_out27), .Q(register_27_q), .clk(in_7), .clr(in_2));
  Register #(.width(32)) register_28 (.D(in_1), .en(decoder_1_out28), .Q(register_28_q), .clk(in_7), .clr(in_2));
  Register #(.width(32)) register_29 (.D(in_1), .en(decoder_1_out29), .Q(register_29_q), .clk(in_7), .clr(in_2));
  Register #(.width(32)) register_30 (.D(in_1), .en(decoder_1_out30), .Q(register_30_q), .clk(in_7), .clr(in_2));
  Register #(.width(32)) register_31 (.D(in_1), .en(decoder_1_out31), .Q(register_31_q), .clk(in_7), .clr(in_2));
  Multiplexer #(.select(5), .width(32)) multiplexer_1 (
    .in0({32{1'b0}}), .in1(register_1_q), .in2(register_2_q), .in3(register_3_q), .in4(register_4_q),
    .in5(out_8), .in6(register_6_q), .in7(register_7_q), .in8(register_8_q), .in9(register_9_q),
    .in10(register_10_q), .in11(register_11_q), .in12(register_12_q), .in13(register_13_q),
    .in14(register_14_q), .in15(register_15_q), .in16(register_16_q), .in17(register_17_q),
    .in18(register_18_q), .in19(register_19_q), .in20(register_20_q), .in21(register_21_q),
    .in22(register_22_q), .in23(register_23_q), .in24(register_24_q), .in25(register_25_q),
    .in26(register_26_q), .in27(register_27_q), .in28(register_28_q), .in29(register_29_q),
    .in30(register_30_q), .in31(register_31_q), .out(out_9), .sel(in_4));  // open: en
  Multiplexer #(.select(5), .width(32)) multiplexer_2 (
    .in0({32{1'b0}}), .in1(register_1_q), .in2(register_2_q), .in3(register_3_q), .in4(register_4_q),
    .in5(out_8), .in6(register_6_q), .in7(register_7_q), .in8(register_8_q), .in9(register_9_q),
    .in10(register_10_q), .in11(register_11_q), .in12(register_12_q), .in13(register_13_q),
    .in14(register_14_q), .in15(register_15_q), .in16(register_16_q), .in17(register_17_q),
    .in18(register_18_q), .in19(register_19_q), .in20(register_20_q), .in21(register_21_q),
    .in22(register_22_q), .in23(register_23_q), .in24(register_24_q), .in25(register_25_q),
    .in26(register_26_q), .in27(register_27_q), .in28(register_28_q), .in29(register_29_q),
    .in30(register_30_q), .in31(register_30_q), .out(out_10), .sel(in_6));  // open: en
endmodule
